# Fritzing sketch neopixel strip and wemos mini (saved by Fritzing 0.9.3b)

parts:
  NEOPIXEL1 = Neopixel Strip -- Black (30/m)
  WeMos_D1_Mini1 = WeMos D1 Mini

nets:
  +5V: NEOPIXEL1.+5V, WeMos_D1_Mini1.3V3
  N1: NEOPIXEL1.DI, WeMos_D1_Mini1.D8
  N2: NEOPIXEL1.GND, WeMos_D1_Mini1.G

custom parts:
  Neopixel Strip -- Black (30/m): Neopixel Strip, Black, 30 pixels per meter.
