# Fritzing sketch wemos and PIR (saved by Fritzing 0.9.2b)

parts:
  WeMos_D1_Mini1 = WeMos D1 Mini
  PIR1 = PIR sensor

nets:
  5V: WeMos_D1_Mini1.5V, PIR1.VDD
  N1: WeMos_D1_Mini1.D7, PIR1.SIG
  N2: WeMos_D1_Mini1.G, PIR1.GND
