# Fritzing sketch wemos and TM1637 (saved by Fritzing 0.9.2b)

parts:
  Grove1 = Grove 4 Digit Display
  WeMos_D1_Mini1 = WeMos D1 Mini

nets:
  N1: Grove1.GND, WeMos_D1_Mini1.G
  VCC: Grove1.VCC, WeMos_D1_Mini1.3V3
  N2: Grove1.DIO, WeMos_D1_Mini1.D5
  N3: Grove1.CLK, WeMos_D1_Mini1.D6

// code stored in the sketch: TM1637ino.ino
#include <TM1637Display.h>

const int CLK = 3; //Set the CLK pin connection to the display
const int DIO = 2; //Set the DIO pin connection to the display

int numCounter = 0;

TM1637Display display(CLK, DIO);  //set up the 4-Digit Display.

void setup()
{
  display.setBrightness(0x0a);  //set the diplay to maximum brightness
}


void loop()
{
  for(numCounter = 0; numCounter < 1000; numCounter++)  //Iterate numCounter
  {
    display.showNumberDec(numCounter); //Display the numCounter value;
    delay(1000);
  }
}
