# Fritzing sketch wemos and force sensor (saved by Fritzing 0.9.2b)
breadboards: 1

parts:
  J1 = Basic Force Sensing Resistor (FSR) [package=THT]
  R1 = Resistor [tolerance=±5% resistance=3.3k package=THT]
  WeMos_D1_Mini1 = WeMos D1 Mini

nets:
  N1: J1.pin_0, WeMos_D1_Mini1.3V3
  N2: J1.pin_1, R1.Pin_0, WeMos_D1_Mini1.A0
  N3: R1.Pin_1, WeMos_D1_Mini1.G
