# Fritzing sketch wemos and hcsr04 (saved by Fritzing 0.9.2b)

parts:
  WeMos_D1_Mini1 = WeMos D1 Mini
  Part1 = SRF05 Ultrasonic Rangefinder

nets:
  5V: WeMos_D1_Mini1.5V, Part1.VCC
  N1: WeMos_D1_Mini1.D6, Part1.Trig
  N2: WeMos_D1_Mini1.D7, Part1.Echo
  N3: WeMos_D1_Mini1.G, Part1.GND
