# Fritzing sketch wemos and max7219  (saved by Fritzing 0.9.2b)

parts:
  WeMos_D1_Mini1 = WeMos D1 Mini
  Part1 = Matrix LED de 8x8 basada en MAX7219

nets:
  3V3: WeMos_D1_Mini1.3V3, Part1.VCC
  N1: WeMos_D1_Mini1.D4, Part1.CS
  N2: WeMos_D1_Mini1.D5, Part1.CLK
  N3: WeMos_D1_Mini1.D7, Part1.DIN
  N4: WeMos_D1_Mini1.G, Part1.GND
