# Fritzing sketch wemos and tmp36 (saved by Fritzing 0.9.3b)
breadboards: 1

parts:
  T1 = TMP36 Temperature Sensor [package="TO92 [THT]"]
  WeMos_D1_Mini1 = WeMos D1 Mini

nets:
  N1: T1.+Vs, WeMos_D1_Mini1.3V3
  N2: T1.Vout, WeMos_D1_Mini1.A0
  N3: T1.GND, WeMos_D1_Mini1.G
