# Fritzing sketch wemos and ws2812 (saved by Fritzing 0.9.2b)

parts:
  WeMos_D1_Mini1 = WeMos D1 Mini
  Part1 = ws2812b [package="smd 2812b"]

nets:
  3V3: WeMos_D1_Mini1.3V3, Part1.VSS
  N1: WeMos_D1_Mini1.D2, Part1.DIN
  N2: WeMos_D1_Mini1.G, Part1.VDD
