# Fritzing sketch wemos mini and ds18b20 (saved by Fritzing 0.9.2b)
breadboards: 1

parts:
  WeMos_D1_Mini1 = WeMos D1 Mini
  DS1 = DS18B20 1-Wire Temperature Sensor [part_number=DS18B20]
  R1 = Resistor [tolerance=±5% resistance=4.7k package=THT]

nets:
  5V: WeMos_D1_Mini1.5V, WeMos_D1_Mini1.D4, DS1.VDD, R1.Pin_1
  N1: WeMos_D1_Mini1.G, DS1.GND
  N2: DS1.DQ, R1.Pin_0
